// Digital circuit ALU.dig as structural Verilog
module ALU (
  input  [7:0] in_1
);

  wire [7:0] shift_l_1_out_8bits, shift_r_1_out_8bits;

  Shift_R shift_r_1 (.In_8bits(in_1), .Out_8bits(shift_r_1_out_8bits));  // open: Enable
  Shift_L shift_l_1 (.In_8bits(in_1), .Out_8bits(shift_l_1_out_8bits));  // open: Enable
  LED led_1 (.in(shift_r_1_out_8bits[0]));
  LED led_2 (.in(shift_r_1_out_8bits[1]));
  LED led_3 (.in(shift_r_1_out_8bits[2]));
  LED led_4 (.in(shift_r_1_out_8bits[3]));
  LED led_5 (.in(shift_r_1_out_8bits[4]));
  LED led_6 (.in(shift_r_1_out_8bits[5]));
  LED led_7 (.in(shift_r_1_out_8bits[6]));
  LED led_8 (.in(shift_r_1_out_8bits[7]));
  LED led_9 (.in(shift_l_1_out_8bits[0]));
  LED led_10 (.in(shift_l_1_out_8bits[1]));
  LED led_11 (.in(shift_l_1_out_8bits[2]));
  LED led_12 (.in(shift_l_1_out_8bits[3]));
  LED led_13 (.in(shift_l_1_out_8bits[4]));
  LED led_14 (.in(shift_l_1_out_8bits[5]));
  LED led_15 (.in(shift_l_1_out_8bits[6]));
  LED led_16 (.in(shift_l_1_out_8bits[7]));
endmodule
